# Fritzing sketch assembly (saved by Fritzing 0.9.2b)
breadboards: 1

parts:
  Part1 = Arduino Nano (Rev3.0)
  Part2 = Thumb Joystick
  Part3 = Thumb Joystick
  U1 = SWITCH_SPDT [package=kps-1290]
  U2 = SWITCH_SPDT [package=kps-1290]
  R1 = Resistor [tolerance=±5% resistance=1k package="0402 [SMD]"]
  R2 = Resistor [tolerance=±5% resistance=1k package="0402 [SMD]"]

nets:
  GND: Part1.GND, Part2.GND, Part3.GND, R1.Pin_1, R2.Pin_1
  N1: Part1.D2, U2.P, R2.Pin_0
  N2: Part1.D3, U1.P, R1.Pin_0
  VCC: Part1.5V, Part2.VCC, Part3.VCC, U1.O, U2.O
  N3: Part1.A5, Part2.VERT
  N4: Part1.A4, Part2.HORZ
  N5: Part1.A1, Part3.VERT
  N6: Part1.A0, Part3.HORZ
